// Logisim project cpu.circ as structural Verilog: 1 circuit, main circuit cpu
module cpu (
  input  clk,
  input  [31:0] Instruction,
  input  [31:0] MemReadData,
  output [31:0] MemAddress,
  output [31:0] ProgramCounter,
  output [31:0] ra,
  output [31:0] sp,
  output [31:0] t0,
  output [31:0] t1,
  output [31:0] t2,
  output [31:0] s0,
  output [31:0] s1,
  output [31:0] a0,
  output [3:0] MemWriteMask,
  output [31:0] MemWriteData
);

  wire BSel, RegWEn;
  wire [1:0] WBSel;
  wire [2:0] control_logic_1_immsel;
  wire [3:0] ALUSel;
  wire [31:0] A, adder_1_out, ALUResult, B, B1, B2, WB;

  Register #(.width(32)) PC (.D(adder_1_out), .clk(clk), .Q(ProgramCounter));  // open: en, clr
  Adder #(.width(32)) adder_1 (.a(ProgramCounter), .b(32'h4), .out(adder_1_out));  // open: cin, cout
  control_logic control_logic_1 (
    .Instruction(Instruction), .RegWEn(RegWEn), .ImmSel(control_logic_1_immsel), .BSel(BSel),
    .ALUSel(ALUSel), .WBSel(WBSel));  // open: BrEq, BrLt, PCSel, BrUn, ASel, MemWEn
  regfile regfile_1 (
    .ReadIndex1(Instruction[19:15]), .ReadIndex2(Instruction[24:20]), .WriteIndex(Instruction[11:7]),
    .WriteData(WB), .RegWEn(1'b1), .clk(clk), .ra(ra), .sp(sp), .t0(t0), .t1(t1), .t2(t2), .s0(s0), .s1(s1),
    .a0(a0), .ReadData1(A), .ReadData2(B1));
  imm_gen imm_gen_1 (.Instruction(Instruction), .ImmSel(control_logic_1_immsel), .Immediate(B2));
  Multiplexer #(.width(32)) multiplexer_1 (.in0(B1), .in1(B2), .out(B), .sel(1'b1));
  alu alu_1 (.A(A), .B(B), .ALUSel(ALUSel), .ALUResult(ALUResult));
  Multiplexer #(.select(2), .width(32)) multiplexer_2 (.in0(ALUResult), .out(WB), .sel(2'b00));  // open: in1, in2, in3
  // branch_comp branch_comp_1: pin names not known
  // partial_store partial_store_1: pin names not known
  // partial_load partial_load_1: pin names not known

  // Notes on the sheet:
  //   To IMEM
  //   IMEM (do **NOT** move this)
  //   From IMEM
  //   Inputs/Outputs for testing. Do **NOT** move these.
  //   To DMEM
  //   DMEM (do **NOT** move this)
  //   From DMEM
endmodule
